// Logisim project control-logic.circ as structural Verilog: 1 circuit, main circuit control_logic
module control_logic (
  input  [31:0] Instruction,
  input  BrEq,
  input  BrLt,
  output PCSel,
  output RegWEn,
  output [2:0] ImmSel,
  output BrUn,
  output ASel,
  output BSel,
  output [3:0] ALUSel,
  output MemWEn,
  output [1:0] WBSel
);

  wire and_1_out, and_2_out, and_3_out, and_4_out, and_5_out, and_6_out, and_7_out, and_8_out, and_10_out,
       and_11_out, and_12_out, and_13_out, and_14_out, and_15_out, and_16_out, comparator_1_eq,
       comparator_2_eq, comparator_3_eq, comparator_4_eq, comparator_5_eq, comparator_6_eq, comparator_7_eq,
       comparator_8_eq, comparator_9_eq, comparator_10_eq, comparator_11_eq, comparator_12_eq,
       comparator_13_eq, comparator_14_eq, comparator_15_eq, comparator_16_eq, comparator_17_eq,
       comparator_18_eq, comparator_19_eq, comparator_20_eq, comparator_21_eq, comparator_22_eq,
       comparator_23_eq, comparator_24_eq, comparator_25_eq, comparator_26_eq, comparator_27_eq,
       comparator_28_eq, comparator_29_eq, comparator_30_eq, comparator_31_eq, comparator_32_eq,
       comparator_33_eq, comparator_34_eq, comparator_35_eq, comparator_36_eq, comparator_37_eq,
       comparator_38_eq, comparator_39_eq, not_1_out, not_2_out, not_3_out, or_2_out, or_4_out, PCSel1,
       PCSel2;
  wire [2:0] priority_encoder_1_out, priority_encoder_2_out, priority_encoder_3_out;
  wire [3:0] priority_encoder_4_p13;
  wire [5:0] adder_1_out, adder_2_out, adder_3_out, adder_4_out, adder_5_out, bit_extender_1_out,
       bit_extender_2_out, bit_extender_3_out, bit_extender_4_out, bit_extender_5_out, bit_extender_6_out,
       or_1_out, ROMInputB, ROMInputI, ROMInputI2, ROMInputIOther, ROMInputR, ROMInputS;
  wire [15:14] rom_1_data;

  Comparator #(.width(3)) comparator_1 (.a(3'b000), .b(Instruction[14:12]), .eq(comparator_1_eq));  // open: gt, lt
  Comparator #(.width(3)) comparator_2 (.a(3'b001), .b(Instruction[14:12]), .eq(comparator_2_eq));  // open: gt, lt
  Comparator #(.width(3)) comparator_3 (.a(3'b010), .b(Instruction[14:12]), .eq(comparator_3_eq));  // open: gt, lt
  Comparator #(.width(3)) comparator_4 (.a(3'b100), .b(Instruction[14:12]), .eq(comparator_4_eq));  // open: gt, lt
  Comparator #(.width(7)) comparator_5 (.a({7{1'b0}}), .b(Instruction[31:25]), .eq(comparator_5_eq));  // open: gt, lt
  Comparator #(.width(3)) comparator_6 (.a(3'b101), .b(Instruction[14:12]), .eq(comparator_6_eq));  // open: gt, lt
  Comparator #(.width(7)) comparator_7 (.a(7'b0100000), .b(Instruction[31:25]), .eq(comparator_7_eq));  // open: gt, lt
  Comparator #(.width(3)) comparator_8 (.a(3'b110), .b(Instruction[14:12]), .eq(comparator_8_eq));  // open: gt, lt
  Comparator #(.width(3)) comparator_9 (.a(3'b111), .b(Instruction[14:12]), .eq(comparator_9_eq));  // open: gt, lt
  Comparator #(.width(3)) comparator_10 (.a(3'b000), .b(Instruction[14:12]), .eq(comparator_10_eq));  // open: gt, lt
  Comparator #(.width(3)) comparator_11 (.a(3'b001), .b(Instruction[14:12]), .eq(comparator_11_eq));  // open: gt, lt
  Comparator #(.width(3)) comparator_12 (.a(3'b100), .b(Instruction[14:12]), .eq(comparator_12_eq));  // open: gt, lt
  Comparator #(.width(3)) comparator_13 (.a(3'b101), .b(Instruction[14:12]), .eq(comparator_13_eq));  // open: gt, lt
  Comparator #(.width(3)) comparator_14 (.a(3'b110), .b(Instruction[14:12]), .eq(comparator_14_eq));  // open: gt, lt
  Comparator #(.width(3)) comparator_15 (.a(3'b111), .b(Instruction[14:12]), .eq(comparator_15_eq));  // open: gt, lt
  assign bit_extender_1_out = {{3{1'b0}}, Instruction[14:12]};  // Bit_Extender bit_extender_1
  assign bit_extender_2_out = {{3{1'b0}}, Instruction[14:12]};  // Bit_Extender bit_extender_2
  assign or_1_out = ROMInputI | ROMInputR | ROMInputB | ROMInputI2 | ROMInputS | ROMInputIOther;  // OR_Gate or_1, 6 bits wide
  and and_1 (and_1_out, comparator_5_eq, comparator_6_eq);
  and and_2 (and_2_out, comparator_6_eq, comparator_7_eq);
  Adder #(.width(6)) adder_1 (.a(6'b001100), .b(bit_extender_1_out), .out(adder_1_out));  // open: cin, cout
  Comparator #(.width(7)) comparator_16 (.a(7'b0000011), .b(Instruction[6:0]), .eq(comparator_16_eq));  // open: gt, lt
  Adder #(.width(6)) adder_2 (.a(6'b010111), .b(bit_extender_2_out), .out(adder_2_out));  // open: cin, cout
  Comparator #(.width(7)) comparator_17 (.a(7'b0100011), .b(Instruction[6:0]), .eq(comparator_17_eq));  // open: gt, lt
  ROM #(.addrWidth(6), .dataWidth(16)) rom_1 (
    .addr(or_1_out), .data({rom_1_data, WBSel, MemWEn, ALUSel, BSel, ASel, BrUn, ImmSel, RegWEn}));
  not not_1 (not_1_out, BrEq);
  not not_2 (not_2_out, BrLt);
  not not_3 (not_3_out, BrLt);
  Multiplexer #(.width(6)) multiplexer_1 (
    .in0({6{1'b0}}), .in1(adder_1_out), .out(ROMInputI2), .sel(comparator_16_eq));  // open: en
  Multiplexer #(.width(6)) multiplexer_2 (
    .in0({6{1'b0}}), .in1(adder_2_out), .out(ROMInputS), .sel(comparator_17_eq));  // open: en
  Priority_Encoder priority_encoder_1 (
    .in0(comparator_1_eq), .in1(comparator_2_eq), .in2(comparator_3_eq), .in3(comparator_4_eq),
    .in4(and_1_out), .in5(and_2_out), .in6(comparator_8_eq), .in7(comparator_9_eq),
    .out(priority_encoder_1_out));  // open: en_in, gs, en_out
  Priority_Encoder priority_encoder_2 (
    .in0(comparator_10_eq), .in1(comparator_11_eq), .in2(comparator_12_eq), .in3(comparator_13_eq),
    .in4(comparator_14_eq), .in5(comparator_15_eq), .in6(1'b0), .in7(1'b0), .out(priority_encoder_2_out));  // open: en_in, gs, en_out
  and and_3 (and_3_out, comparator_10_eq, BrEq);
  and and_4 (and_4_out, comparator_11_eq, not_1_out);
  and and_5 (and_5_out, comparator_12_eq, BrLt);
  and and_6 (and_6_out, comparator_13_eq, not_2_out);
  and and_7 (and_7_out, comparator_14_eq, BrLt);
  and and_8 (and_8_out, comparator_15_eq, not_3_out);
  Adder #(.width(6)) adder_3 (.a(6'b001111), .b(bit_extender_3_out), .out(adder_3_out));  // open: cin, cout
  assign bit_extender_3_out = {{3{1'b0}}, priority_encoder_1_out};  // Bit_Extender bit_extender_3
  Adder #(.width(6)) adder_4 (.a(6'b011010), .b(bit_extender_4_out), .out(adder_4_out));  // open: cin, cout
  assign bit_extender_4_out = {{3{1'b0}}, priority_encoder_2_out};  // Bit_Extender bit_extender_4
  Multiplexer #(.width(6)) multiplexer_3 (
    .in0({6{1'b0}}), .in1(adder_3_out), .out(ROMInputI), .sel(comparator_18_eq));  // open: en
  Comparator #(.width(7)) comparator_18 (.a(7'b0010011), .b(Instruction[6:0]), .eq(comparator_18_eq));  // open: gt, lt
  Multiplexer #(.width(6)) multiplexer_4 (
    .in0({6{1'b0}}), .in1(adder_4_out), .out(ROMInputB), .sel(comparator_19_eq));  // open: en
  Comparator #(.width(7)) comparator_19 (.a(7'b1100011), .b(Instruction[6:0]), .eq(comparator_19_eq));  // open: gt, lt
  and and_9 (PCSel1, comparator_19_eq, or_2_out);
  or or_2 (or_2_out, and_3_out, and_4_out, and_5_out, and_6_out, and_7_out, and_8_out);
  Comparator #(.width(7)) comparator_20 (.a(7'b0010111), .b(Instruction[6:0]), .eq(comparator_20_eq));  // open: gt, lt
  Comparator #(.width(7)) comparator_21 (.a(7'b0110111), .b(Instruction[6:0]), .eq(comparator_21_eq));  // open: gt, lt
  Comparator #(.width(7)) comparator_22 (.a(7'b1101111), .b(Instruction[6:0]), .eq(comparator_22_eq));  // open: gt, lt
  Comparator #(.width(7)) comparator_23 (.a(7'b1100111), .b(Instruction[6:0]), .eq(comparator_23_eq));  // open: gt, lt
  or or_3 (PCSel, PCSel1, PCSel2);
  assign bit_extender_5_out = {{4{1'b0}}, priority_encoder_3_out[1:0]};  // Bit_Extender bit_extender_5
  Priority_Encoder priority_encoder_3 (
    .in2(comparator_20_eq), .in3(comparator_21_eq), .in4(comparator_22_eq), .in5(comparator_23_eq),
    .out(priority_encoder_3_out));  // open: in0, in1, in6, in7, en_in, gs, en_out
  or or_4 (or_4_out, comparator_23_eq, comparator_22_eq, comparator_21_eq, comparator_20_eq);
  or or_5 (PCSel2, comparator_23_eq, comparator_22_eq);
  Comparator #(.width(3)) comparator_24 (.a(3'b000), .b(Instruction[14:12]), .eq(comparator_24_eq));  // open: gt, lt
  Comparator #(.width(7)) comparator_25 (.a({7{1'b0}}), .b(Instruction[31:25]), .eq(comparator_25_eq));  // open: gt, lt
  Comparator #(.width(7)) comparator_26 (
    .a(7'b0000001), .b(Instruction[31:25]), .eq(comparator_26_eq));  // open: gt, lt
  Comparator #(.width(7)) comparator_27 (
    .a(7'b0100000), .b(Instruction[31:25]), .eq(comparator_27_eq));  // open: gt, lt
  Comparator #(.width(7)) comparator_28 (.a({7{1'b0}}), .b(Instruction[31:25]), .eq(comparator_28_eq));  // open: gt, lt
  Comparator #(.width(3)) comparator_29 (.a(3'b001), .b(Instruction[14:12]), .eq(comparator_29_eq));  // open: gt, lt
  Comparator #(.width(7)) comparator_30 (
    .a(7'b0000001), .b(Instruction[31:25]), .eq(comparator_30_eq));  // open: gt, lt
  Comparator #(.width(3)) comparator_31 (.a(3'b011), .b(Instruction[14:12]), .eq(comparator_31_eq));  // open: gt, lt
  Comparator #(.width(3)) comparator_32 (.a(3'b010), .b(Instruction[14:12]), .eq(comparator_32_eq));  // open: gt, lt
  Comparator #(.width(3)) comparator_33 (.a(3'b100), .b(Instruction[14:12]), .eq(comparator_33_eq));  // open: gt, lt
  Comparator #(.width(7)) comparator_34 (.a({7{1'b0}}), .b(Instruction[31:25]), .eq(comparator_34_eq));  // open: gt, lt
  Comparator #(.width(3)) comparator_35 (.a(3'b101), .b(Instruction[14:12]), .eq(comparator_35_eq));  // open: gt, lt
  Comparator #(.width(7)) comparator_36 (
    .a(7'b0100000), .b(Instruction[31:25]), .eq(comparator_36_eq));  // open: gt, lt
  Comparator #(.width(3)) comparator_37 (.a(3'b110), .b(Instruction[14:12]), .eq(comparator_37_eq));  // open: gt, lt
  Comparator #(.width(3)) comparator_38 (.a(3'b111), .b(Instruction[14:12]), .eq(comparator_38_eq));  // open: gt, lt
  Adder #(.width(6)) adder_5 (.a(6'b100000), .b(bit_extender_5_out), .out(adder_5_out));  // open: cin, cout
  and and_10 (and_10_out, comparator_24_eq, comparator_25_eq);
  and and_11 (and_11_out, comparator_24_eq, comparator_26_eq);
  and and_12 (and_12_out, comparator_24_eq, comparator_27_eq);
  and and_13 (and_13_out, comparator_28_eq, comparator_29_eq);
  and and_14 (and_14_out, comparator_29_eq, comparator_30_eq);
  and and_15 (and_15_out, comparator_34_eq, comparator_35_eq);
  and and_16 (and_16_out, comparator_35_eq, comparator_36_eq);
  Multiplexer #(.width(6)) multiplexer_5 (
    .in0({6{1'b0}}), .in1(adder_5_out), .out(ROMInputIOther), .sel(or_4_out));  // open: en
  // Priority_Encoder priority_encoder_4: pin names not known; wires that end beside it: and_10_out, and_11_out, and_12_out, and_13_out, and_14_out, comparator_31_eq, comparator_32_eq, comparator_33_eq, and_15_out, and_16_out, comparator_37_eq, comparator_38_eq, priority_encoder_4_p13
  assign bit_extender_6_out = {{2{1'b0}}, priority_encoder_4_p13};  // Bit_Extender bit_extender_6
  Multiplexer #(.width(6)) multiplexer_6 (
    .in0({6{1'b0}}), .in1(bit_extender_6_out), .out(ROMInputR), .sel(comparator_39_eq));  // open: en
  Comparator #(.width(7)) comparator_39 (.a(7'b0110011), .b(Instruction[6:0]), .eq(comparator_39_eq));  // open: gt, lt
  // Pins of 2 and 3 bits meet at priority_encoder_3_out

  // Other names for the same wires on the sheet: opcode[6:0] = Instruction[6:0]; rd[4:0] = Instruction[11:7];
  //   funct3[2:0] = Instruction[14:12]; rs1[4:0] = Instruction[19:15]; immI[11:0] = Instruction[31:20];
  //   funct7[6:0] = Instruction[31:25]

  // Notes on the sheet:
  //   INPUTS to your circuit
  //   contents of rom_1 (hex, n*v repeats v):
  //   1003 1403 1603 1083 1483 1583 1103 1203 1283 1683 1303 1383 41 41 41 1041 10c1 1141 1241 12c1 16c1
  //   1341 13c1 1842 1842 1842 4*64 74 74 1067 17c7 2069 2041
  //   ROM FOR CONTROL LOGIC
  //   DON'T CHANGE THE LOCATIONS OF THE INPUTS AND OUTPUTS!
  //   This is only if you choose to do the ROM option
  //   OUTPUT from your circuit
endmodule
