// Logisim project control_logic.circ as structural Verilog: 1 circuit, main circuit control_logic
module control_logic (
  input  [31:0] inst,
  input  BrEq,
  input  BrLt,
  input  [6:0] in_4,
  input  [2:0] in_5,
  input  [6:0] in_6,
  output PCSel,
  output RegWEn,
  output [2:0] ImmSel,
  output BrUn,
  output ASel,
  output BSel,
  output [3:0] ALUSel,
  output MemRW,
  output [1:0] WBSel,
  output CSRSel,
  output CSRWen
);

  wire and_1_out, and_2_out, and_3_out, and_4_out, and_5_out, and_6_out, and_7_out, and_8_out, and_9_out,
       B_TYPE, comparator_3_eq, comparator_18_eq, comparator_19_eq, comparator_20_eq, comparator_21_eq,
       comparator_22_eq, comparator_23_eq, comparator_24_eq, comparator_25_eq, f3_0, f3_1, f3_2, f3_3, f3_4,
       f3_5, f3_6, f3_7, f7_0, f7_01, f7_10, I_A, I_TYPE, JI_TYPE, or_2_out, priority_encoder_6_en_out,
       R_TYPE, S_TYPE;
  wire [1:0] priority_encoder_2_out, priority_encoder_5_out;
  wire [2:0] CHOOSE, priority_encoder_3_out, priority_encoder_4_out, priority_encoder_6_out;
  wire [3:0] priority_encoder_1_out;
  wire [5:0] B_INPUTA, bit_extender_2_out, bit_extender_3_out, bit_extender_4_out, bit_extender_5_out,
       I_INPUTA, multiplexer_1_out, multiplexer_2_out, R_INPUT, S_INPUTA, UJI_INPUTA;
  wire [15:14] rom_1_data;

  Comparator #(.width(7)) comparator_1 (.a(in_4), .b(7'b0110011), .eq(R_TYPE));  // open: gt, lt
  Comparator #(.width(7)) comparator_2 (.a(in_4), .b(7'b0000011), .eq(I_A));  // open: gt, lt
  Comparator #(.width(7)) comparator_3 (.a(in_4), .b(7'b0010011), .eq(comparator_3_eq));  // open: gt, lt
  Comparator #(.width(7)) comparator_4 (.a(in_4), .b(7'b0100011), .eq(S_TYPE));  // open: gt, lt
  Comparator #(.width(7)) comparator_5 (.a(in_4), .b(7'b1100011), .eq(B_TYPE));  // open: gt, lt
  Comparator #(.width(3)) comparator_6 (.a(in_4[2:0]), .b(3'b011), .eq(JI_TYPE));  // open: gt, lt
  or or_1 (I_TYPE, I_A, comparator_3_eq);
  and and_1 (and_1_out, f3_0, f7_0);
  and and_2 (and_2_out, f3_0, f7_01);
  and and_3 (and_3_out, f3_0, f7_10);
  and and_4 (and_4_out, f3_1, f7_0);
  and and_5 (and_5_out, f3_1, f7_01);
  and and_6 (and_6_out, f3_5, f7_0);
  and and_7 (and_7_out, f3_5, f7_10);
  Priority_Encoder #(.select(4)) priority_encoder_1 (
    .in0(and_1_out), .in1(and_2_out), .in2(and_3_out), .in3(and_4_out), .in4(and_5_out), .in5(f3_3),
    .in6(f3_2), .in7(f3_4), .in8(and_6_out), .in9(and_7_out), .in10(f3_6), .in11(f3_7),
    .out(priority_encoder_1_out), .en_in(R_TYPE));  // open: in12, in13, in14, in15, gs, en_out
  assign R_INPUT = {{2{1'b0}}, priority_encoder_1_out};  // Bit_Extender bit_extender_1
  Multiplexer #(.enable("false"), .select(3), .width(6)) multiplexer_1 (
    .in0(R_INPUT), .in1(I_INPUTA), .in2(S_INPUTA), .in3(B_INPUTA), .in4(UJI_INPUTA), .out(multiplexer_1_out),
    .sel(CHOOSE));  // open: in5, in6, in7
  Comparator #(.width(3)) comparator_7 (.a(3'b000), .b(in_5), .eq(f3_0));  // open: gt, lt
  Comparator #(.width(3)) comparator_8 (.a(in_5), .b(3'b001), .eq(f3_1));  // open: gt, lt
  Comparator #(.width(3)) comparator_9 (.a(in_5), .b(3'b010), .eq(f3_2));  // open: gt, lt
  Comparator #(.width(3)) comparator_10 (.a(in_5), .b(3'b011), .eq(f3_3));  // open: gt, lt
  Comparator #(.width(3)) comparator_11 (.a(in_5), .b(3'b100), .eq(f3_4));  // open: gt, lt
  Comparator #(.width(3)) comparator_12 (.a(in_5), .b(3'b101), .eq(f3_5));  // open: gt, lt
  Comparator #(.width(3)) comparator_13 (.a(in_5), .b(3'b110), .eq(f3_6));  // open: gt, lt
  Comparator #(.width(3)) comparator_14 (.a(in_5), .b(3'b111), .eq(f3_7));  // open: gt, lt
  ROM #(.addrWidth(6), .dataWidth(16)) rom_1 (
    .addr(multiplexer_1_out), .data({rom_1_data, WBSel, MemRW, ALUSel, BSel, ASel, BrUn, ImmSel, RegWEn}));
  Priority_Encoder #(.select(2)) priority_encoder_2 (
    .in0(f3_0), .in1(f3_1), .in2(f3_2), .out(priority_encoder_2_out), .en_in(S_TYPE));  // open: in3, gs, en_out
  and and_8 (and_8_out, f7_0, f3_5);
  and and_9 (and_9_out, f3_5, f7_10);
  assign bit_extender_2_out = {{4{1'b0}}, priority_encoder_2_out};  // Bit_Extender bit_extender_2
  Priority_Encoder priority_encoder_3 (
    .in0(f3_0), .in1(f3_1), .in2(f3_4), .in3(f3_5), .in4(f3_6), .in5(f3_7), .out(priority_encoder_3_out),
    .en_in(B_TYPE));  // open: in6, in7, gs, en_out
  Adder #(.width(6)) adder_1 (.a(6'b010111), .b(bit_extender_2_out), .out(S_INPUTA));  // open: cin, cout
  assign bit_extender_3_out = {{3{1'b0}}, priority_encoder_4_out};  // Bit_Extender bit_extender_3
  Priority_Encoder priority_encoder_4 (
    .in0(f3_0), .in1(f3_1), .in2(f3_2), .in3(f3_4), .in4(and_8_out), .in5(and_9_out), .in6(f3_6), .in7(f3_7),
    .out(priority_encoder_4_out), .en_in(I_TYPE));  // open: gs, en_out
  Adder #(.width(6)) adder_2 (.a(6'b011010), .b(bit_extender_4_out), .out(B_INPUTA));  // open: cin, cout
  assign bit_extender_4_out = {{3{1'b0}}, priority_encoder_3_out};  // Bit_Extender bit_extender_4
  Comparator #(.width(7)) comparator_15 (.a(in_6), .b({7{1'b0}}), .eq(f7_0));  // open: gt, lt
  Comparator #(.width(7)) comparator_16 (.a(in_6), .b(7'b0000001), .eq(f7_01));  // open: gt, lt
  Comparator #(.width(7)) comparator_17 (.a(in_6), .b(7'b0100000), .eq(f7_10));  // open: gt, lt
  Multiplexer #(.enable("false"), .width(6)) multiplexer_2 (
    .in0(6'b001111), .in1(6'b001100), .out(multiplexer_2_out), .sel(I_A));
  Adder #(.width(6)) adder_3 (.a(multiplexer_2_out), .b(bit_extender_3_out), .out(I_INPUTA));  // open: cin, cout
  Comparator #(.width(7)) comparator_18 (.a(in_4), .b(7'b0010111), .eq(comparator_18_eq));  // open: gt, lt
  Comparator #(.width(7)) comparator_19 (.a(in_4), .b(7'b0110111), .eq(comparator_19_eq));  // open: gt, lt
  Comparator #(.width(7)) comparator_20 (.a(in_4), .b(7'b1101111), .eq(comparator_20_eq));  // open: gt, lt
  Comparator #(.width(7)) comparator_21 (.a(in_4), .b(7'b1100111), .eq(comparator_21_eq));  // open: gt, lt
  Comparator #(.width(7)) comparator_22 (.a(in_4), .b(7'b0010111), .eq(comparator_22_eq));  // open: gt, lt
  Comparator #(.width(7)) comparator_23 (.a(in_4), .b(7'b0110111), .eq(comparator_23_eq));  // open: gt, lt
  Comparator #(.width(7)) comparator_24 (.a(in_4), .b(7'b1101111), .eq(comparator_24_eq));  // open: gt, lt
  Comparator #(.width(7)) comparator_25 (.a(in_4), .b(7'b1100111), .eq(comparator_25_eq));  // open: gt, lt
  or or_2 (or_2_out, comparator_18_eq, comparator_19_eq, comparator_20_eq, comparator_21_eq);
  Priority_Encoder #(.select(2)) priority_encoder_5 (
    .in0(comparator_22_eq), .in1(comparator_23_eq), .in2(comparator_24_eq), .in3(comparator_25_eq),
    .out(priority_encoder_5_out));  // open: gs, en_out, en_in
  Priority_Encoder priority_encoder_6 (
    .in0(R_TYPE), .in1(I_TYPE), .in2(S_TYPE), .in3(B_TYPE), .in4(or_2_out), .in5(1'b0), .in6(1'b0),
    .in7(1'b0), .out(priority_encoder_6_out), .en_out(priority_encoder_6_en_out));  // open: en_in, gs
  assign bit_extender_5_out = {{4{1'b0}}, priority_encoder_5_out};  // Bit_Extender bit_extender_5
  Multiplexer #(.enable("false"), .width(3)) multiplexer_3 (
    .in0(priority_encoder_6_out), .in1(3'b000), .out(CHOOSE), .sel(priority_encoder_6_en_out));
  Adder #(.width(6)) adder_4 (.a(6'b100000), .b(bit_extender_5_out), .out(UJI_INPUTA));  // open: cin, cout

  assign PCSel = 1'b0;

  // Other names for the same wires on the sheet: funct3[2:0] = in_5; funct7[6:0] = in_6; rd[4:0] = inst[11:7];
  //   rs1[4:0] = inst[19:15]; immI[11:0] = inst[31:20]; opcode[6:0] = in_4

  // Notes on the sheet:
  //   INPUTS to your circuit
  //   DON'T CHANGE THE LOCATIONS OF THE INPUTS AND OUTPUTS!
  //   OUTPUT from your circuit
  //   contents of rom_1 (hex, n*v repeats v):
  //   1003 1403 1603 1083 1483 1583 1103 1203 1283 1683 1303 1383 41 41 41 1041 10c1 1141 1241 12c1 16c1
  //   1341 13c1 1842 1842 1842 4*64 74 74 1067 17c7 2069 2041
endmodule
