// Logisim project cpu.circ as structural Verilog: 1 circuit, main circuit cpu
module cpu (
  input  clk,
  input  [31:0] INSTRUCTION,
  input  [31:0] READ_DATA,
  output [31:0] WRITE_ADDRESS,
  output [31:0] PROGRAM_COUNTER,
  output [31:0] ra,
  output [31:0] sp,
  output [31:0] t0,
  output [31:0] t1,
  output [31:0] t2,
  output [31:0] s0,
  output [31:0] s1,
  output [31:0] a0,
  output [31:0] tohost,
  output [3:0] WRITE_ENABLE,
  output [31:0] WRITE_DATA
);

  wire ASel, BrEq, BrLt, BrUn, BSel, CSRSel, CSRWen, MemRW, PCSel, RW;
  wire [1:0] WBSel;
  wire [2:0] ImSel;
  wire [3:0] ALUSel;
  wire [31:0] imm_gen_1_imm, inst, multiplexer_1_out, multiplexer_2_out, multiplexer_3_out, PC_add, RD1, RD2,
       regfile_1_read_data_1, WD;

  Adder #(.width(32)) adder_1 (.a(PROGRAM_COUNTER), .b(32'h4), .out(PC_add));  // open: cin, cout
  Multiplexer #(.enable("false"), .width(32)) multiplexer_1 (
    .in0(PC_add), .in1(WRITE_ADDRESS), .out(multiplexer_1_out), .sel(PCSel));
  Register #(.width(32)) register_1 (.D(INSTRUCTION), .clk(clk), .Q(inst));  // open: en, clr
  Register #(.width(32)) PC (.D(multiplexer_1_out), .clk(clk), .Q(PROGRAM_COUNTER));  // open: en, clr
  control_logic control_logic_1 (
    .CSRWen(CSRWen), .PCSel(PCSel), .RegWEn(RW), .ImmSel(ImSel), .BrUn(BrUn), .ASel(ASel), .BSel(BSel),
    .ALUSel(ALUSel), .MemRW(MemRW), .WBSel(WBSel), .CSRSel(CSRSel), .inst(inst), .BrEq(BrEq), .BrLt(BrLt));  // open: in_4, in_5, in_6
  regfile regfile_1 (
    .rs1(inst[19:15]), .rs2(inst[24:20]), .rd(inst[11:7]), .Write_Data(WD), .RegWEn(RW), .clk(clk), .ra(ra),
    .sp(sp), .t0(t0), .t1(t1), .t2(t2), .s0(s0), .s1(s1), .a0(a0), .Read_Data_1(regfile_1_read_data_1),
    .Read_Data_2(WRITE_DATA));
  imm_gen imm_gen_1 (.inst(inst), .ImmSel(ImSel), .imm(imm_gen_1_imm));
  Multiplexer #(.enable("false"), .width(32)) multiplexer_2 (
    .in0(WRITE_DATA), .in1(imm_gen_1_imm), .out(multiplexer_2_out), .sel(BSel));
  Multiplexer #(.enable("false"), .width(32)) multiplexer_3 (
    .in0(regfile_1_read_data_1), .in1(PROGRAM_COUNTER), .out(multiplexer_3_out), .sel(ASel));
  alu alu_1 (.Result(WRITE_ADDRESS), .A(multiplexer_3_out), .B(multiplexer_2_out), .ALUSel(ALUSel));
  branch_comp branch_comp_1 (.rs1(RD1), .rs2(RD2), .BrUn(BrUn), .BrEq(BrEq), .BrLt(BrLt));
  Multiplexer #(.enable("false"), .select(2), .width(32)) multiplexer_4 (
    .in0(READ_DATA), .in1(WRITE_ADDRESS), .in2(PC_add), .out(WD), .sel(WBSel));  // open: in3
  // csr csr_1: pin names not known; wires that end beside it: tohost

  // Other names for the same wires on the sheet: ALUResult[31:0] = WRITE_ADDRESS; rd[4:0] = inst[11:7];
  //   rs1[4:0] = inst[19:15]; rs2[4:0] = inst[24:20]; PC[31:0] = PROGRAM_COUNTER

  // Notes on the sheet:
  //   Output to IMEM
  //   IMEM (do **NOT** move this)
  //   Inputs from IMEM
  //   It is OK to move the PC, RegFile, ALU, MEM, Branch Comp, Imm Gen, and Control Logic to wherever is most convenient for you when constructing your CPU, and to delete this text
  //   Inputs/Outputs for testing. Do **NOT** move these.
  //   Outputs To DMEM
  //   DMEM (do **NOT** move this)
  //   Inputs From DMEM
endmodule
